// Logisim project stack_logical_easy.circ as structural Verilog: 30 circuits, main circuit stack
module test (
  input  D,
  input  C
);

  wire d_ff_1_q, d_ff_2_q, d_trigger_back_1_q, d_trigger_back_2_q, d_trigger_front_1_q, d_trigger_front_2_q,
       d_trigger_high_1_q, d_trigger_high_2_q;

  D_Flip_Flop #(.trigger("high")) d_ff_1 (.D(D), .clk(C), .Q(d_ff_1_q));  // open: Qn, preset, reset
  D_Flip_Flop #(.trigger("high")) d_ff_2 (.D(d_ff_1_q), .clk(C), .Q(d_ff_2_q));  // open: Qn, preset, reset
  D_Flip_Flop #(.trigger("high")) d_ff_3 (.D(d_ff_2_q), .clk(C));  // open: Q, Qn, preset, reset
  D_trigger_high d_trigger_high_1 (.D(D), .C(C), .Q(d_trigger_high_1_q));
  D_trigger_back d_trigger_back_1 (.D(D), .C(C), .Q(d_trigger_back_1_q));
  D_trigger_front d_trigger_front_1 (.D(D), .C(C), .Q(d_trigger_front_1_q));
  D_trigger_high d_trigger_high_2 (.D(d_trigger_high_1_q), .C(C), .Q(d_trigger_high_2_q));
  D_trigger_back d_trigger_back_2 (.D(d_trigger_back_1_q), .C(C), .Q(d_trigger_back_2_q));
  D_trigger_front d_trigger_front_2 (.D(d_trigger_front_1_q), .C(C), .Q(d_trigger_front_2_q));
  D_trigger_high d_trigger_high_3 (.D(d_trigger_high_2_q), .C(C));  // open: Q
  D_trigger_back d_trigger_back_3 (.D(d_trigger_back_2_q), .C(C));  // open: Q
  D_trigger_front d_trigger_front_3 (.D(d_trigger_front_2_q), .C(C));  // open: Q
endmodule

module stack (
  input  CLK,
  input  RESET,
  input  [1:0] COMMAND,
  input  [2:0] INDEX,
  input  [3:0] IDATA,
  output [3:0] ODATA
);

  wire b_to_d_demux_1_i1, b_to_d_demux_1_i2, b_to_d_demux_1_i3, or_1_out, or_2_out, por_1_out;
  wire [3:0] dddd_and_a_1_q, dddd_and_a_2_q, head_1_index, or_3_out, quad_sub_mod_e_1_out_3;

  B_to_D_DEMUX b_to_d_demux_1 (
    .D(CLK), .S(COMMAND), .i1(b_to_d_demux_1_i1), .i2(b_to_d_demux_1_i2), .i3(b_to_d_demux_1_i3));  // open: i0
  or or_1 (or_1_out, RESET, por_1_out);
  POR por_1 (.out(por_1_out));
  DDDD_AND_A dddd_and_a_1 (.D(4'b0100), .A(b_to_d_demux_1_i2), .Q(dddd_and_a_1_q));
  DDDD_AND_A dddd_and_a_2 (.D({1'b0, INDEX}), .A(b_to_d_demux_1_i3), .Q(dddd_and_a_2_q));
  or or_2 (or_2_out, b_to_d_demux_1_i3, b_to_d_demux_1_i2);
  assign or_3_out = dddd_and_a_1_q | dddd_and_a_2_q;  // OR_Gate or_3, 4 bits wide
  // Probe on head_1_index
  HEAD head_1 (
    .INCR_IND(b_to_d_demux_1_i1), .DECR_IND(b_to_d_demux_1_i2), .CLK(CLK), .RESET(or_1_out),
    .INDEX(head_1_index));
  quad_SUB_mod_E quad_sub_mod_e_1 (.X(head_1_index), .Y(or_3_out), .out_3(quad_sub_mod_e_1_out_3));
  MEMORY memory_1 (
    .GET(or_2_out), .SET(b_to_d_demux_1_i1), .INDEX(quad_sub_mod_e_1_out_3), .IDATA(IDATA), .RESET(or_1_out),
    .ODATA(ODATA));

  // Notes on the sheet:
  //   00 - nop
  //   01 - push
  //   10 - pop
  //   11 - get
  //   get
  //   pop
  //   push
endmodule

module MEMORY (
  input  GET,
  input  SET,
  input  [3:0] INDEX,
  input  [3:0] IDATA,
  input  RESET,
  output [3:0] ODATA
);

  wire c_to_h_demux_1_i0, c_to_h_demux_1_i1, c_to_h_demux_1_i2, c_to_h_demux_1_i3, c_to_h_demux_1_i4,
       c_to_h_demux_2_i0, c_to_h_demux_2_i1, c_to_h_demux_2_i2, c_to_h_demux_2_i3, c_to_h_demux_2_i4,
       kostyl_1_out_2, kostyl_2_out_2, kostyl_3_out_2, kostyl_4_out_2, not_1_out, or_1_out, or_2_out,
       or_3_out, or_4_out, or_5_out;
  wire [3:0] dddd_and_a_1_q, dddd_and_a_2_q, dddd_and_a_3_q, dddd_and_a_4_q, dddd_and_a_5_q, dddd_and_a_6_q,
       dddd_and_a_7_q, dddd_and_a_8_q, dddd_and_a_9_q, dddd_and_a_10_q, or_6_out, or_7_out, or_8_out,
       quad_memory_1_odata, quad_memory_2_odata, quad_memory_3_odata, quad_memory_4_odata,
       quad_memory_5_odata;

  kostyl kostyl_1 (.in_1(SET), .out_2(kostyl_1_out_2));
  kostyl kostyl_2 (.in_1(kostyl_1_out_2), .out_2(kostyl_2_out_2));
  kostyl kostyl_3 (.in_1(kostyl_2_out_2), .out_2(kostyl_3_out_2));
  kostyl kostyl_4 (.in_1(kostyl_3_out_2), .out_2(kostyl_4_out_2));
  C_to_H_DEMUX c_to_h_demux_1 (
    .S(INDEX), .D(kostyl_4_out_2), .i0(c_to_h_demux_1_i0), .i1(c_to_h_demux_1_i1), .i2(c_to_h_demux_1_i2),
    .i3(c_to_h_demux_1_i3), .i4(c_to_h_demux_1_i4));  // open: i5, i6, i7
  not not_1 (not_1_out, RESET);
  or or_1 (or_1_out, c_to_h_demux_1_i0, ~not_1_out);  // OR_Gate
  or or_2 (or_2_out, c_to_h_demux_1_i1, ~not_1_out);  // OR_Gate
  or or_3 (or_3_out, c_to_h_demux_1_i2, ~not_1_out);  // OR_Gate
  or or_4 (or_4_out, c_to_h_demux_1_i3, ~not_1_out);  // OR_Gate
  or or_5 (or_5_out, c_to_h_demux_1_i4, ~not_1_out);  // OR_Gate
  DDDD_AND_A dddd_and_a_1 (.D(IDATA), .A(not_1_out), .Q(dddd_and_a_1_q));
  DDDD_AND_A dddd_and_a_2 (.D(IDATA), .A(not_1_out), .Q(dddd_and_a_2_q));
  DDDD_AND_A dddd_and_a_3 (.D(IDATA), .A(not_1_out), .Q(dddd_and_a_3_q));
  DDDD_AND_A dddd_and_a_4 (.D(IDATA), .A(not_1_out), .Q(dddd_and_a_4_q));
  DDDD_AND_A dddd_and_a_5 (.D(IDATA), .A(not_1_out), .Q(dddd_and_a_5_q));
  C_to_H_DEMUX c_to_h_demux_2 (
    .S(INDEX), .D(GET), .i0(c_to_h_demux_2_i0), .i1(c_to_h_demux_2_i1), .i2(c_to_h_demux_2_i2),
    .i3(c_to_h_demux_2_i3), .i4(c_to_h_demux_2_i4));  // open: i5, i6, i7
  // Probe on quad_memory_1_odata
  quad_memory quad_memory_1 (.IDATA(dddd_and_a_1_q), .SET(or_1_out), .ODATA(quad_memory_1_odata));
  // Probe on quad_memory_2_odata
  quad_memory quad_memory_2 (.IDATA(dddd_and_a_2_q), .SET(or_2_out), .ODATA(quad_memory_2_odata));
  // Probe on quad_memory_3_odata
  quad_memory quad_memory_3 (.IDATA(dddd_and_a_3_q), .SET(or_3_out), .ODATA(quad_memory_3_odata));
  // Probe on quad_memory_4_odata
  quad_memory quad_memory_4 (.IDATA(dddd_and_a_4_q), .SET(or_4_out), .ODATA(quad_memory_4_odata));
  // Probe on quad_memory_5_odata
  quad_memory quad_memory_5 (.IDATA(dddd_and_a_5_q), .SET(or_5_out), .ODATA(quad_memory_5_odata));
  DDDD_AND_A dddd_and_a_6 (.D(quad_memory_1_odata), .A(c_to_h_demux_2_i0), .Q(dddd_and_a_6_q));
  assign or_6_out = dddd_and_a_6_q | dddd_and_a_7_q;  // OR_Gate or_6, 4 bits wide
  DDDD_AND_A dddd_and_a_7 (.D(quad_memory_2_odata), .A(c_to_h_demux_2_i1), .Q(dddd_and_a_7_q));
  DDDD_AND_A dddd_and_a_8 (.D(quad_memory_3_odata), .A(c_to_h_demux_2_i2), .Q(dddd_and_a_8_q));
  assign or_7_out = dddd_and_a_8_q | dddd_and_a_9_q;  // OR_Gate or_7, 4 bits wide
  DDDD_AND_A dddd_and_a_9 (.D(quad_memory_4_odata), .A(c_to_h_demux_2_i3), .Q(dddd_and_a_9_q));
  DDDD_AND_A dddd_and_a_10 (.D(quad_memory_5_odata), .A(c_to_h_demux_2_i4), .Q(dddd_and_a_10_q));
  assign or_8_out = or_6_out | or_7_out;  // OR_Gate or_8, 4 bits wide
  assign ODATA = or_8_out | dddd_and_a_10_q;  // OR_Gate or_9, 4 bits wide
endmodule

module HEAD (
  input  INCR_IND,
  input  DECR_IND,
  input  CLK,
  input  RESET,
  output [3:0] INDEX
);

  wire and_1_out, kostyl_1_out_2, not_1_out, or_1_out, or_3_out;
  wire [3:0] dddd_and_a_1_q, dddd_and_a_2_q, dddd_and_a_3_q, dddd_and_a_4_q, decrement_mod_e_1_odata,
       increment_mod_e_1_odata, or_2_out, or_4_out;

  DDDD_AND_A dddd_and_a_1 (.D(increment_mod_e_1_odata), .A(INCR_IND), .Q(dddd_and_a_1_q));
  DDDD_AND_A dddd_and_a_2 (.D(decrement_mod_e_1_odata), .A(DECR_IND), .Q(dddd_and_a_2_q));
  or or_1 (or_1_out, INCR_IND, DECR_IND);
  assign or_2_out = dddd_and_a_1_q | dddd_and_a_2_q;  // OR_Gate or_2, 4 bits wide
  not not_1 (not_1_out, RESET);
  and and_1 (and_1_out, or_1_out, CLK);
  DDDD_AND_A dddd_and_a_3 (.D(or_2_out), .A(not_1_out), .Q(dddd_and_a_3_q));
  DDDD_AND_A dddd_and_a_4 (.A(RESET), .Q(dddd_and_a_4_q));  // open: D
  or or_3 (or_3_out, and_1_out, RESET);
  kostyl kostyl_1 (.in_1(or_3_out), .out_2(kostyl_1_out_2));
  // Probe on or_4_out
  assign or_4_out = dddd_and_a_3_q | dddd_and_a_4_q;  // OR_Gate or_4, 4 bits wide
  // Probe on INDEX
  quad_memory_front quad_memory_front_1 (.IDATA(or_4_out), .SET(kostyl_1_out_2), .ODATA(INDEX));
  // Probe on increment_mod_e_1_odata
  increment_mod_E increment_mod_e_1 (.IDATA(INDEX), .ODATA(increment_mod_e_1_odata));
  decrement_mod_E decrement_mod_e_1 (.IDATA(INDEX), .ODATA(decrement_mod_e_1_odata));
  // Probe on decrement_mod_e_1_odata
endmodule

module increment_mod_E (
  input  [3:0] IDATA,
  output [3:0] ODATA
);

  wire and_1_out, not_1_out;
  wire [3:0] dddd_and_a_1_q, dddd_and_a_2_q, increment_1_odata;

  // NoConnect on IDATA[3]
  and and_1 (and_1_out, increment_1_odata[0], ~increment_1_odata[1], increment_1_odata[2]);  // AND_Gate
  increment increment_1 (.IDATA({1'b0, IDATA[2:0]}), .ODATA(increment_1_odata));
  not not_1 (not_1_out, and_1_out);
  DDDD_AND_A dddd_and_a_1 (.D(increment_1_odata), .A(not_1_out), .Q(dddd_and_a_1_q));
  assign ODATA = dddd_and_a_1_q | dddd_and_a_2_q;  // OR_Gate or_1, 4 bits wide
  DDDD_AND_A dddd_and_a_2 (.D(4'b0000), .A(and_1_out), .Q(dddd_and_a_2_q));

  // Notes on the sheet:
  //   // избавляемся от старшего бита
  //    (на всякий случай...)
  //   if (DATA == 101) DATA = 0;
endmodule

module decrement_mod_E (
  input  [3:0] IDATA,
  output [3:0] ODATA
);

  wire and_1_out, not_1_out;
  wire [3:0] dddd_and_a_1_q, dddd_and_a_2_q, decrement_1_odata;

  // NoConnect on IDATA[3]
  and and_1 (and_1_out, decrement_1_odata[0], decrement_1_odata[1], decrement_1_odata[2]);
  decrement decrement_1 (.IDATA({1'b0, IDATA[2:0]}), .ODATA(decrement_1_odata));
  not not_1 (not_1_out, and_1_out);
  DDDD_AND_A dddd_and_a_1 (.D(decrement_1_odata), .A(not_1_out), .Q(dddd_and_a_1_q));
  assign ODATA = dddd_and_a_1_q | dddd_and_a_2_q;  // OR_Gate or_1, 4 bits wide
  DDDD_AND_A dddd_and_a_2 (.D(4'b0100), .A(and_1_out), .Q(dddd_and_a_2_q));

  // Notes on the sheet:
  //   // избавляемся от старшего бита
  //    (на всякий случай...)
  //   if (DATA == 0) DATA = 100;
endmodule

module quad_SUM (
  input  [3:0] X,
  input  [3:0] Y,
  output [3:0] SUM,
  output C
);

  wire sum_1_c, sum_2_c, sum_3_c;

  SUM sum_1 (.X(1'b0), .Y(X[0]), .Z(Y[0]), .S(SUM[0]), .C(sum_1_c));
  SUM sum_2 (.X(sum_1_c), .Y(X[1]), .Z(Y[1]), .S(SUM[1]), .C(sum_2_c));
  SUM sum_3 (.X(sum_2_c), .Y(X[2]), .Z(Y[2]), .S(SUM[2]), .C(sum_3_c));
  SUM sum_4 (.X(sum_3_c), .Y(X[3]), .Z(Y[3]), .S(SUM[3]), .C(C));

  // Notes on the sheet:
  //   // Бит переноса
endmodule

module quad_SUB (
  input  [3:0] in_1,
  input  [3:0] in_2,
  output [3:0] out_3
);

  wire quad_sum_1_c, quad_sum_2_c;
  wire [3:0] not_1_out, quad_sum_1_sum;

  assign not_1_out = ~in_2;  // NOT_Gate not_1, 4 bits wide
  quad_SUM quad_sum_1 (.X(in_1), .Y(not_1_out), .SUM(quad_sum_1_sum), .C(quad_sum_1_c));
  // NoConnect on quad_sum_1_c
  quad_SUM quad_sum_2 (.X(quad_sum_1_sum), .Y(4'b0001), .SUM(out_3), .C(quad_sum_2_c));
  // NoConnect on quad_sum_2_c
endmodule

module quad_SUM_mod_E (
  input  [3:0] X,
  input  [3:0] Y,
  output [3:0] out_3
);

  wire quad_sum_1_c;
  wire [3:0] quad_sum_1_sum;

  quad_SUM quad_sum_1 (.X(X), .Y(Y), .SUM(quad_sum_1_sum), .C(quad_sum_1_c));
  // NoConnect on quad_sum_1_c
  mod_E mod_e_1 (.X(quad_sum_1_sum), .X_mod_5(out_3));
endmodule

module quad_SUB_mod_E (
  input  [3:0] X,
  input  [3:0] Y,
  output [3:0] out_3
);

  wire [3:0] quad_sub_1_out_3;

  quad_SUB quad_sub_1 (.in_1(X), .in_2(Y), .out_3(quad_sub_1_out_3));
  mod_E mod_e_1 (.X(quad_sub_1_out_3), .X_mod_5(out_3));
endmodule

module mod_E (
  input  [3:0] X,
  output [3:0] X_mod_5
);

  wire n0_out, n1_out, n2_out, n3_out, n4_out, n5_out, n6_out, n7_out, n8_out, n9_out, n10_out, n11_out,
       n12_out, n13_out, n14_out, n15_out;
  wire [3:0] dddd_and_a_1_q, dddd_and_a_2_q, dddd_and_a_3_q, dddd_and_a_4_q, dddd_and_a_5_q, dddd_and_a_6_q,
       dddd_and_a_7_q, dddd_and_a_8_q, dddd_and_a_9_q, dddd_and_a_10_q, dddd_and_a_11_q, dddd_and_a_12_q,
       dddd_and_a_13_q, dddd_and_a_14_q, dddd_and_a_15_q, dddd_and_a_16_q, or_1_out, or_2_out, or_3_out,
       or_4_out, or_5_out, or_6_out, or_7_out, or_8_out, or_9_out, or_10_out, or_11_out, or_12_out,
       or_13_out, or_14_out;

  and n0 (n0_out, ~X[0], ~X[1], ~X[2], ~X[3]);  // AND_Gate
  and n1 (n1_out, X[0], ~X[1], ~X[2], ~X[3]);  // AND_Gate
  and n2 (n2_out, ~X[0], X[1], ~X[2], ~X[3]);  // AND_Gate
  and n3 (n3_out, X[0], X[1], ~X[2], ~X[3]);  // AND_Gate
  and n4 (n4_out, ~X[0], ~X[1], X[2], ~X[3]);  // AND_Gate
  and n5 (n5_out, X[0], ~X[1], X[2], ~X[3]);  // AND_Gate
  and n6 (n6_out, ~X[0], X[1], X[2], ~X[3]);  // AND_Gate
  and n7 (n7_out, X[0], X[1], X[2], ~X[3]);  // AND_Gate
  and n8 (n8_out, ~X[0], ~X[1], ~X[2], X[3]);  // AND_Gate
  and n9 (n9_out, X[0], ~X[1], ~X[2], X[3]);  // AND_Gate
  and n10 (n10_out, ~X[0], X[1], ~X[2], X[3]);  // AND_Gate
  and n11 (n11_out, X[0], X[1], ~X[2], X[3]);  // AND_Gate
  and n12 (n12_out, ~X[0], ~X[1], X[2], X[3]);  // AND_Gate
  and n13 (n13_out, X[0], ~X[1], X[2], X[3]);  // AND_Gate
  and n14 (n14_out, ~X[0], X[1], X[2], X[3]);  // AND_Gate
  and n15 (n15_out, X[0], X[1], X[2], X[3]);
  DDDD_AND_A dddd_and_a_1 (.D(4'b0000), .A(n0_out), .Q(dddd_and_a_1_q));
  DDDD_AND_A dddd_and_a_2 (.D(4'b0001), .A(n1_out), .Q(dddd_and_a_2_q));
  DDDD_AND_A dddd_and_a_3 (.D(4'b0010), .A(n2_out), .Q(dddd_and_a_3_q));
  DDDD_AND_A dddd_and_a_4 (.D(4'b0011), .A(n3_out), .Q(dddd_and_a_4_q));
  DDDD_AND_A dddd_and_a_5 (.D(4'b0100), .A(n4_out), .Q(dddd_and_a_5_q));
  DDDD_AND_A dddd_and_a_6 (.D(4'b0000), .A(n5_out), .Q(dddd_and_a_6_q));
  DDDD_AND_A dddd_and_a_7 (.D(4'b0001), .A(n6_out), .Q(dddd_and_a_7_q));
  DDDD_AND_A dddd_and_a_8 (.D(4'b0001), .A(n7_out), .Q(dddd_and_a_8_q));
  DDDD_AND_A dddd_and_a_9 (.D(4'b0010), .A(n8_out), .Q(dddd_and_a_9_q));
  DDDD_AND_A dddd_and_a_10 (.D(4'b0011), .A(n9_out), .Q(dddd_and_a_10_q));
  DDDD_AND_A dddd_and_a_11 (.D(4'b0100), .A(n10_out), .Q(dddd_and_a_11_q));
  DDDD_AND_A dddd_and_a_12 (.D(4'b0000), .A(n11_out), .Q(dddd_and_a_12_q));
  DDDD_AND_A dddd_and_a_13 (.D(4'b0001), .A(n12_out), .Q(dddd_and_a_13_q));
  DDDD_AND_A dddd_and_a_14 (.D(4'b0010), .A(n13_out), .Q(dddd_and_a_14_q));
  DDDD_AND_A dddd_and_a_15 (.D(4'b0011), .A(n14_out), .Q(dddd_and_a_15_q));
  DDDD_AND_A dddd_and_a_16 (.D(4'b0100), .A(n15_out), .Q(dddd_and_a_16_q));
  assign or_1_out = dddd_and_a_1_q | dddd_and_a_2_q;  // OR_Gate or_1, 4 bits wide
  assign or_2_out = or_1_out | or_3_out;  // OR_Gate or_2, 4 bits wide
  assign or_3_out = dddd_and_a_3_q | dddd_and_a_4_q;  // OR_Gate or_3, 4 bits wide
  assign or_4_out = dddd_and_a_5_q | dddd_and_a_6_q;  // OR_Gate or_4, 4 bits wide
  assign or_5_out = or_4_out | or_6_out;  // OR_Gate or_5, 4 bits wide
  assign or_6_out = dddd_and_a_7_q | dddd_and_a_8_q;  // OR_Gate or_6, 4 bits wide
  assign or_7_out = dddd_and_a_9_q | dddd_and_a_10_q;  // OR_Gate or_7, 4 bits wide
  assign or_8_out = or_7_out | or_9_out;  // OR_Gate or_8, 4 bits wide
  assign or_9_out = dddd_and_a_11_q | dddd_and_a_12_q;  // OR_Gate or_9, 4 bits wide
  assign or_10_out = dddd_and_a_13_q | dddd_and_a_14_q;  // OR_Gate or_10, 4 bits wide
  assign or_11_out = or_10_out | or_12_out;  // OR_Gate or_11, 4 bits wide
  assign or_12_out = dddd_and_a_15_q | dddd_and_a_16_q;  // OR_Gate or_12, 4 bits wide
  assign or_13_out = or_2_out | or_5_out;  // OR_Gate or_13, 4 bits wide
  assign or_14_out = or_8_out | or_11_out;  // OR_Gate or_14, 4 bits wide
  assign X_mod_5 = or_13_out | or_14_out;  // OR_Gate or_15, 4 bits wide

  // Notes on the sheet:
  //   Извините.
endmodule

module quad_memory (
  input  [3:0] IDATA,
  input  SET,
  output [3:0] ODATA
);

  wire or_1_out, por_1_out;

  or or_1 (or_1_out, SET, por_1_out);
  POR por_1 (.out(por_1_out));
  D_trigger_high d_trigger_high_1 (.D(IDATA[0]), .C(or_1_out), .Q(ODATA[0]));
  D_trigger_high d_trigger_high_2 (.D(IDATA[1]), .C(or_1_out), .Q(ODATA[1]));
  D_trigger_high d_trigger_high_3 (.D(IDATA[2]), .C(or_1_out), .Q(ODATA[2]));
  D_trigger_high d_trigger_high_4 (.D(IDATA[3]), .C(or_1_out), .Q(ODATA[3]));
endmodule

module quad_memory_front (
  input  [3:0] IDATA,
  input  SET,
  output [3:0] ODATA
);

  wire or_1_out, por_1_out;

  or or_1 (or_1_out, SET, por_1_out);
  POR por_1 (.out(por_1_out));
  D_trigger_front d_trigger_front_1 (.D(IDATA[0]), .C(or_1_out), .Q(ODATA[0]));
  D_trigger_front d_trigger_front_2 (.D(IDATA[1]), .C(or_1_out), .Q(ODATA[1]));
  D_trigger_front d_trigger_front_3 (.D(IDATA[2]), .C(or_1_out), .Q(ODATA[2]));
  D_trigger_front d_trigger_front_4 (.D(IDATA[3]), .C(or_1_out), .Q(ODATA[3]));
endmodule

module quad_memory_back (
  input  [3:0] IDATA,
  input  SET,
  output [3:0] ODATA
);

  wire or_1_out, por_1_out;

  or or_1 (or_1_out, SET, por_1_out);
  POR por_1 (.out(por_1_out));
  D_trigger_back d_trigger_back_1 (.D(IDATA[0]), .C(or_1_out), .Q(ODATA[0]));
  D_trigger_back d_trigger_back_2 (.D(IDATA[1]), .C(or_1_out), .Q(ODATA[1]));
  D_trigger_back d_trigger_back_3 (.D(IDATA[2]), .C(or_1_out), .Q(ODATA[2]));
  D_trigger_back d_trigger_back_4 (.D(IDATA[3]), .C(or_1_out), .Q(ODATA[3]));
endmodule

module DH_to_DC_MUX (
  input  S0,
  input  S1,
  input  S2,
  input  [3:0] i0,
  input  [3:0] i1,
  input  [3:0] i2,
  input  [3:0] i3,
  input  [3:0] i4,
  input  [3:0] i5,
  input  [3:0] i6,
  input  [3:0] i7,
  output [3:0] Q
);

  wire c_to_h_decoder_1_q0, c_to_h_decoder_1_q1, c_to_h_decoder_1_q2, c_to_h_decoder_1_q3,
       c_to_h_decoder_1_q4, c_to_h_decoder_1_q5, c_to_h_decoder_1_q6, c_to_h_decoder_1_q7;
  wire [3:0] dddd_and_a_1_q, dddd_and_a_2_q, dddd_and_a_3_q, dddd_and_a_4_q, dddd_and_a_5_q, dddd_and_a_6_q,
       dddd_and_a_7_q, dddd_and_a_8_q, or_1_out, or_2_out, or_3_out, or_4_out, or_5_out, or_6_out;

  C_to_H_decoder c_to_h_decoder_1 (
    .S1(S1), .S2(S2), .S0(S0), .Q0(c_to_h_decoder_1_q0), .Q1(c_to_h_decoder_1_q1), .Q2(c_to_h_decoder_1_q2),
    .Q3(c_to_h_decoder_1_q3), .Q4(c_to_h_decoder_1_q4), .Q5(c_to_h_decoder_1_q5), .Q6(c_to_h_decoder_1_q6),
    .Q7(c_to_h_decoder_1_q7));
  DDDD_AND_A dddd_and_a_1 (.D(i0), .A(c_to_h_decoder_1_q0), .Q(dddd_and_a_1_q));
  DDDD_AND_A dddd_and_a_2 (.D(i1), .A(c_to_h_decoder_1_q1), .Q(dddd_and_a_2_q));
  DDDD_AND_A dddd_and_a_3 (.D(i2), .A(c_to_h_decoder_1_q2), .Q(dddd_and_a_3_q));
  DDDD_AND_A dddd_and_a_4 (.D(i3), .A(c_to_h_decoder_1_q3), .Q(dddd_and_a_4_q));
  DDDD_AND_A dddd_and_a_5 (.D(i4), .A(c_to_h_decoder_1_q4), .Q(dddd_and_a_5_q));
  DDDD_AND_A dddd_and_a_6 (.D(i5), .A(c_to_h_decoder_1_q5), .Q(dddd_and_a_6_q));
  DDDD_AND_A dddd_and_a_7 (.D(i6), .A(c_to_h_decoder_1_q6), .Q(dddd_and_a_7_q));
  DDDD_AND_A dddd_and_a_8 (.D(i7), .A(c_to_h_decoder_1_q7), .Q(dddd_and_a_8_q));
  assign or_1_out = dddd_and_a_1_q | dddd_and_a_2_q;  // OR_Gate or_1, 4 bits wide
  assign or_2_out = dddd_and_a_3_q | dddd_and_a_4_q;  // OR_Gate or_2, 4 bits wide
  assign or_3_out = dddd_and_a_5_q | dddd_and_a_6_q;  // OR_Gate or_3, 4 bits wide
  assign or_4_out = dddd_and_a_7_q | dddd_and_a_8_q;  // OR_Gate or_4, 4 bits wide
  assign or_5_out = or_1_out | or_2_out;  // OR_Gate or_5, 4 bits wide
  assign or_6_out = or_3_out | or_4_out;  // OR_Gate or_6, 4 bits wide
  assign Q = or_5_out | or_6_out;  // OR_Gate or_7, 4 bits wide
endmodule

module DC_to_DH_DEMUX (
  input  [3:0] DDDD,
  input  S0,
  input  S1,
  input  S2,
  output [3:0] DDDD0,
  output [3:0] DDDD1,
  output [3:0] DDDD2,
  output [3:0] DDDD3,
  output [3:0] DDDD4,
  output [3:0] DDDD5,
  output [3:0] DDDD6,
  output [3:0] DDDD7
);

  wire c_to_h_decoder_1_q0, c_to_h_decoder_1_q1, c_to_h_decoder_1_q2, c_to_h_decoder_1_q3,
       c_to_h_decoder_1_q4, c_to_h_decoder_1_q5, c_to_h_decoder_1_q6, c_to_h_decoder_1_q7;

  C_to_H_decoder c_to_h_decoder_1 (
    .S1(S1), .S2(S2), .S0(S0), .Q0(c_to_h_decoder_1_q0), .Q1(c_to_h_decoder_1_q1), .Q2(c_to_h_decoder_1_q2),
    .Q3(c_to_h_decoder_1_q3), .Q4(c_to_h_decoder_1_q4), .Q5(c_to_h_decoder_1_q5), .Q6(c_to_h_decoder_1_q6),
    .Q7(c_to_h_decoder_1_q7));
  DDDD_AND_A dddd_and_a_1 (.D(DDDD), .A(c_to_h_decoder_1_q0), .Q(DDDD0));
  DDDD_AND_A dddd_and_a_2 (.D(DDDD), .A(c_to_h_decoder_1_q1), .Q(DDDD1));
  DDDD_AND_A dddd_and_a_3 (.D(DDDD), .A(c_to_h_decoder_1_q2), .Q(DDDD2));
  DDDD_AND_A dddd_and_a_4 (.D(DDDD), .A(c_to_h_decoder_1_q3), .Q(DDDD3));
  DDDD_AND_A dddd_and_a_5 (.D(DDDD), .A(c_to_h_decoder_1_q4), .Q(DDDD4));
  DDDD_AND_A dddd_and_a_6 (.D(DDDD), .A(c_to_h_decoder_1_q5), .Q(DDDD5));
  DDDD_AND_A dddd_and_a_7 (.D(DDDD), .A(c_to_h_decoder_1_q6), .Q(DDDD6));
  DDDD_AND_A dddd_and_a_8 (.D(DDDD), .A(c_to_h_decoder_1_q7), .Q(DDDD7));
endmodule

module B_to_D_DEMUX (
  input  D,
  input  [1:0] S,
  output i0,
  output i1,
  output i2,
  output i3
);

  wire b_to_d_decoder_1_q0, b_to_d_decoder_1_q1, b_to_d_decoder_1_q2, b_to_d_decoder_1_q3;

  B_to_D_decoder b_to_d_decoder_1 (
    .i0(S[0]), .i1(S[1]), .Q0(b_to_d_decoder_1_q0), .Q1(b_to_d_decoder_1_q1), .Q2(b_to_d_decoder_1_q2),
    .Q3(b_to_d_decoder_1_q3));
  and and_1 (i0, D, b_to_d_decoder_1_q0);
  and and_2 (i1, D, b_to_d_decoder_1_q1);
  and and_3 (i2, D, b_to_d_decoder_1_q2);
  and and_4 (i3, D, b_to_d_decoder_1_q3);
endmodule

module C_to_H_DEMUX (
  input  D,
  input  [3:0] S,
  output i0,
  output i1,
  output i2,
  output i3,
  output i4,
  output i5,
  output i6,
  output i7
);

  wire c_to_h_decoder_1_q0, c_to_h_decoder_1_q1, c_to_h_decoder_1_q2, c_to_h_decoder_1_q3,
       c_to_h_decoder_1_q4, c_to_h_decoder_1_q5, c_to_h_decoder_1_q6, c_to_h_decoder_1_q7, kostyl_1_out_2;

  kostyl kostyl_1 (.in_1(D), .out_2(kostyl_1_out_2));
  C_to_H_decoder c_to_h_decoder_1 (
    .S1(S[1]), .S2(S[2]), .S0(S[0]), .Q0(c_to_h_decoder_1_q0), .Q1(c_to_h_decoder_1_q1),
    .Q2(c_to_h_decoder_1_q2), .Q3(c_to_h_decoder_1_q3), .Q4(c_to_h_decoder_1_q4), .Q5(c_to_h_decoder_1_q5),
    .Q6(c_to_h_decoder_1_q6), .Q7(c_to_h_decoder_1_q7));
  and and_1 (i0, kostyl_1_out_2, c_to_h_decoder_1_q0);
  and and_2 (i1, kostyl_1_out_2, c_to_h_decoder_1_q1);
  and and_3 (i2, kostyl_1_out_2, c_to_h_decoder_1_q2);
  and and_4 (i3, kostyl_1_out_2, c_to_h_decoder_1_q3);
  and and_5 (i4, kostyl_1_out_2, c_to_h_decoder_1_q4);
  and and_6 (i5, kostyl_1_out_2, c_to_h_decoder_1_q5);
  and and_7 (i6, kostyl_1_out_2, c_to_h_decoder_1_q6);
  and and_8 (i7, kostyl_1_out_2, c_to_h_decoder_1_q7);
endmodule

module B_to_D_decoder (
  input  i0,
  input  i1,
  output Q0,
  output Q1,
  output Q2,
  output Q3
);

  and and_1 (Q0, ~i0, ~i1);  // AND_Gate
  and and_2 (Q1, i0, ~i1);  // AND_Gate
  and and_3 (Q2, ~i0, i1);  // AND_Gate
  and and_4 (Q3, i0, i1);
endmodule

module C_to_H_decoder (
  input  S0,
  input  S1,
  input  S2,
  output Q0,
  output Q1,
  output Q2,
  output Q3,
  output Q4,
  output Q5,
  output Q6,
  output Q7
);

  and and_1 (Q0, ~S0, ~S1, ~S2);  // AND_Gate
  and and_2 (Q1, S0, ~S1, ~S2);  // AND_Gate
  and and_3 (Q2, ~S0, S1, ~S2);  // AND_Gate
  and and_4 (Q3, S0, S1, ~S2);  // AND_Gate
  and and_5 (Q4, ~S0, ~S1, S2);  // AND_Gate
  and and_6 (Q5, S0, ~S1, S2);  // AND_Gate
  and and_7 (Q6, ~S0, S1, S2);  // AND_Gate
  and and_8 (Q7, S0, S1, S2);
endmodule

module D_trigger_high (
  input  D,
  input  C,
  output Q
);

  wire not_1_out;

  not not_1 (not_1_out, D);
  RS_trigger rs_trigger_1 (.R(not_1_out), .C(C), .S(D), .Q(Q));  // open: notQ
endmodule

module D_trigger_front (
  input  D,
  input  C,
  output Q
);

  wire not_1_out, not_2_out, rs_trigger_1_notq, rs_trigger_1_q, rs_trigger_2_notq;

  not not_1 (not_1_out, C);
  not not_2 (not_2_out, D);
  RS_trigger rs_trigger_1 (.R(D), .C(not_1_out), .S(not_2_out), .Q(rs_trigger_1_q), .notQ(rs_trigger_1_notq));
  RS_trigger rs_trigger_2 (.R(rs_trigger_1_q), .C(C), .S(rs_trigger_1_notq), .Q(Q), .notQ(rs_trigger_2_notq));
  // NoConnect on rs_trigger_2_notq
endmodule

module D_trigger_back (
  input  D,
  input  C,
  output Q
);

  wire jk_trigger_1_notq, not_1_out;

  not not_1 (not_1_out, D);
  JK_trigger jk_trigger_1 (.J(D), .C(C), .K(not_1_out), .Q(Q), .notQ(jk_trigger_1_notq));
  // NoConnect on jk_trigger_1_notq
endmodule

module JK_trigger (
  input  J,
  input  C,
  input  K,
  output Q,
  output notQ
);

  wire and_1_out, and_2_out, not_1_out, rs_trigger_1_notq, rs_trigger_1_q;

  and and_1 (and_1_out, Q, K);
  and and_2 (and_2_out, J, notQ);
  not not_1 (not_1_out, C);
  RS_trigger rs_trigger_1 (.R(and_2_out), .C(C), .S(and_1_out), .Q(rs_trigger_1_q), .notQ(rs_trigger_1_notq));
  RS_trigger rs_trigger_2 (.R(rs_trigger_1_q), .C(not_1_out), .S(rs_trigger_1_notq), .Q(Q), .notQ(notQ));
endmodule

module RS_trigger (
  input  R,
  input  C,
  input  S,
  output Q,
  output notQ
);

  wire and_1_out, and_2_out, or_1_out, por_1_out;

  and and_1 (and_1_out, R, C);
  and and_2 (and_2_out, C, S);
  POR por_1 (.out(por_1_out));
  or or_1 (or_1_out, and_2_out, por_1_out);
  nor nor_1 (Q, and_1_out, notQ);
  nor nor_2 (notQ, Q, or_1_out);
endmodule

module DDDD_AND_A (
  input  [3:0] D,
  input  A,
  output [3:0] Q
);

  assign Q = D & {4{A}};  // AND_Gate and_1, 4 bits wide
endmodule

module increment (
  input  [3:0] IDATA,
  output [3:0] ODATA
);

  wire quad_sum_1_c;

  quad_SUM quad_sum_1 (.X(IDATA), .Y(4'b0001), .SUM(ODATA), .C(quad_sum_1_c));
  // NoConnect on quad_sum_1_c

  // Notes on the sheet:
  //   // прибавим 1
endmodule

module decrement (
  input  [3:0] IDATA,
  output [3:0] ODATA
);

  wire quad_sum_1_c;

  quad_SUM quad_sum_1 (.X(IDATA), .Y(4'b1111), .SUM(ODATA), .C(quad_sum_1_c));
  // NoConnect on quad_sum_1_c

  // Notes on the sheet:
  //   // прибавим 15 (-1)
endmodule

module SUM (
  input  X,
  input  Y,
  input  Z,
  output S,
  output C
);

  wire and_1_out, and_2_out, xor_1_out;

  xor xor_1 (xor_1_out, X, Y);
  xor xor_2 (S, xor_1_out, Z);
  and and_1 (and_1_out, xor_1_out, Z);
  and and_2 (and_2_out, X, Y);
  or or_1 (C, and_1_out, and_2_out);
endmodule

module kostyl (
  input  in_1,
  output out_2
);

  wire not_1_out, not_2_out, not_3_out, not_4_out, not_5_out, not_6_out, not_7_out, not_8_out, not_9_out,
       not_10_out, not_11_out, not_12_out, not_13_out, not_14_out, not_15_out;

  not not_1 (not_1_out, in_1);
  not not_2 (not_2_out, not_1_out);
  not not_3 (not_3_out, not_2_out);
  not not_4 (not_4_out, not_3_out);
  not not_5 (not_5_out, not_4_out);
  not not_6 (not_6_out, not_5_out);
  not not_7 (not_7_out, not_6_out);
  not not_8 (not_8_out, not_7_out);
  not not_9 (not_9_out, not_8_out);
  not not_10 (not_10_out, not_9_out);
  not not_11 (not_11_out, not_10_out);
  not not_12 (not_12_out, not_11_out);
  not not_13 (not_13_out, not_12_out);
  not not_14 (not_14_out, not_13_out);
  not not_15 (not_15_out, not_14_out);
  not not_16 (out_2, not_15_out);
endmodule
